# Fritzing sketch device (saved by Fritzing 0.9.9b)
breadboards: 2

parts:
  Teensy1 = Teensy 4.0
  LCD1 = 2.8" SPI TFT Module [part_number=MSP2807]
  R1 = Resistor [tolerance=±5% resistance=150 package="2010 [SMD]"]

nets:
  N1: Teensy1.pin_1, Teensy1.pin_32, LCD1.pin2
  N2: Teensy1.pin_13, LCD1.pin6
  N3: Teensy1.pin_14, LCD1.pin9
  N4: Teensy1.pin_20, LCD1.pin7
  N5: Teensy1.pin_26, LCD1.pin4
  N6: Teensy1.pin_27, LCD1.pin5
  N7: Teensy1.pin_28, LCD1.pin3
  N8: Teensy1.pin33, LCD1.pin1, R1.Pin_1
  N9: LCD1.pin8, R1.Pin_0

custom parts:
  Teensy 4.0: The Teensy is a complete USB-based microcontoller development system, in a very small footprint, capable of implementing many types of projects. All programming is done via the USB port. No special programmer is needed, only a standard micro-USB cable and a PC or Macintosh with a USB port.
  2.8" SPI TFT Module: A generic 2.8 inch LCD TFT 320x240 display with touchscreen and SD card slot. Uses the ILI9341 controller, like the Adafruit displays of this size uses.
